# Fritzing sketch circuit board (saved by Fritzing 0.9.3b)
perfboards: 1

parts:
  Part1 = Arduino Nano (Rev3.0)  # not connected
  J3 = screw terminal, 2 pins
  J4 = female pin header, 4 pins [form="♀ (female)"]
  J5 = female pin header, 3 pins [form="♀ (female)"]  # not connected
  J6 = female pin header, 15 pins [form="♀ (female)"]
  J7 = female pin header, 15 pins [form="♀ (female)"]
  J8 = female pin header, 3 pins [form="♀ (female)"]
  J9 = female pin header, 3 pins [form="♀ (female)"]
  Q2 = NPN-Transistor [package="TO92 [THT]"]
  Part2 = KY-021 Mini Magnetic Reed Switch Module [package="Breakout board"]
  Part3 = KY-021 Mini Magnetic Reed Switch Module [package="Breakout board"]

nets:
  N1: J3.pin1, J4.pin3, J6.pin2
  N2: J3.pin2, J6.pin1
  N3: J4.pin1, J7.pin1
  N4: J4.pin4, Q2.E
  VIN: J6.pin4, J8.pin2, J9.pin2, Q2.C, Part2.Vin, Part3.Vin
  N5: J6.pin12, Q2.B
  N6: J7.pin4, J8.pin3, J9.pin3, Part2.-, Part3.-
  N7: J7.pin5, J8.pin1, Part2.S
  N8: J7.pin6, J9.pin1, Part3.S

notes:
  VCC
  GND
  RX
  VIN
  5V
  A0
  TX
  D2
  D3
  GND Bus
  5V Bus
  Support
  Postbox sensor
  Door sensor

custom parts:
  KY-021 Mini Magnetic Reed Switch Module: KY-021 magnetic reed switch module. A reed switch is a magnetic sensor that is normally open and gets closed when exposed to a magnetic field.
