# Fritzing sketch postbox-monitor (saved by Fritzing 0.9.3b)
perfboards: 1

parts:
  VCC1 = 4 x AAA Battery Mount
  R1 = Resistor [tolerance=±5% resistance=1M package=THT]
  R2 = Resistor [tolerance=±5% resistance=1M package=THT]
  R3 = Resistor [tolerance=±5% resistance=1M package=THT]
  R4 = Resistor [tolerance=±5% resistance=1M package=THT]
  D2F1 = D2F-FL Omron Snap Action Limit Switch with Level
  D2F2 = D2F-FL Omron Snap Action Limit Switch with Level

nets:
  N1: VCC1.-, R2.Pin_0, D2F1.NC, D2F2.NC
  N2: VCC1.+, R1.Pin_1
  N3: R1.Pin_0, R2.Pin_1
  N4: R3.Pin_0, D2F2.COM
  N5: R3.Pin_1, R4.Pin_1
  N6: R4.Pin_0, D2F1.COM

notes:
  A2
  Flap
  Door
  A0
  A1
  3V3
  2x 1MΩ
  4.8V
  VCC
  GND

custom parts:
  D2F-FL Omron Snap Action Limit Switch with Level: Snap action switch with stainless steel lever.
