# Fritzing sketch real-installation (saved by Fritzing 0.9.3b)
perfboards: 2

parts:
  VCC2 = 4 x AAA Battery Mount
  R8 = Resistor [tolerance=±5% resistance=1M package=THT]
  R5 = Resistor [tolerance=±5% resistance=1M package=THT]
  D2F2 = D2F-FL Omron Snap Action Limit Switch with Level
  D2F3 = D2F-FL Omron Snap Action Limit Switch with Level
  J6 = female pin header, 2 pins [form="♀ (female)"]
  J7 = female pin header, 2 pins [form="♀ (female)"]
  J8 = female pin header, 2 pins [form="♀ (female)"]
  J9 = female pin header, 6 pins [form="♀ (female)"]
  R9 = Resistor [tolerance=±5% resistance=1M package=THT]
  R10 = Resistor [tolerance=±5% resistance=1M package=THT]

nets:
  N1: VCC2.-, R5.Pin_1, D2F2.NC, D2F3.COM, J6.pin1, J7.pin2, J8.pin2, J9.pin3
  N2: VCC2.+, J8.pin1, J9.pin1, R10.Pin_0
  N3: R8.Pin_0, D2F3.NC, J6.pin2, J9.pin6
  N4: R8.Pin_1, J9.pin2, R9.Pin_1
  N5: R5.Pin_0, J9.pin4, R10.Pin_1
  N6: D2F2.COM, J7.pin1, J9.pin5, R9.Pin_0

notes:
  4.8V
  Door
  Flap
  GND
  VCC
  3V3
  A0
  A2
  A1

custom parts:
  D2F-FL Omron Snap Action Limit Switch with Level: Snap action switch with stainless steel lever.
