# Fritzing sketch postbox-board (saved by Fritzing 0.9.3b)
perfboards: 2

parts:
  VCC2 = 4 x AAA Battery Mount
  R6 = Resistor [tolerance=±5% resistance=1M package=THT]  # not connected
  R7 = Resistor [tolerance=±5% resistance=1M package=THT]  # not connected
  S3 = Pushbutton [package=THT]
  S4 = Pushbutton [package=THT]
  J1 = female pin header, 2 pins [form="♀ (female)"]  # not connected
  J3 = female pin header, 2 pins [form="♀ (female)"]
  J4 = female pin header, 2 pins [form="♀ (female)"]
  J5 = female pin header, 3 pins [form="♀ (female)"]
  J2 = female pin header, 3 pins [form="♀ (female)"]
  R8 = Resistor [tolerance=±5% resistance=1M package=THT]  # not connected
  R5 = Resistor [tolerance=±5% resistance=1M package=THT]  # not connected

nets:
  N1: VCC2.-, J2.pin3
  N2: VCC2.+, J2.pin1
  N3: S3.leg0, S4.leg0, J3.pin1, J4.pin1
  N4: S3.leg1, J4.pin2, J5.pin2
  N5: S4.leg1, J3.pin2, J5.pin1

notes:
  4.8V
  A2
  A0
  Door
  Flap
  A1
  GND
  VCC
  3V3
