# Fritzing sketch postbox-monitor-diagram (saved by Fritzing 0.9.3b)
breadboards: 1

parts:
  Part2 = Arduino Nano (Rev3.0)
  Part3 = KY-021 Mini Magnetic Reed Switch Module [package="Breakout board"]
  Part4 = KY-021 Mini Magnetic Reed Switch Module [package="Breakout board"]
  Part5 = Bluetooth HC-05 Macho
  BAT1 = BC9VPC [package=bc9vpc]
  Q1 = NPN-Transistor [package="TO92 [THT]"]
  R2 = Resistor [tolerance=±5% resistance=1k package="2512 [SMD]"]

nets:
  N1: Part2.D1/TX, Part5.TXD
  N2: Part2.D0/RX, Part5.RXD
  GND: Part2.GND, Part3.-, Part4.-, Part5.GND, BAT1.V-
  N3: Part2.D2, Part4.S
  N4: Part2.D3, Part3.S
  N5: Part2.VIN, BAT1.V+
  VIN: Part2.5V, Part3.Vin, Part4.Vin, Q1.C
  N6: Part2.A0, R2.Pin_0
  N7: Part5.VCC, Q1.E
  N8: Q1.B, R2.Pin_1

custom parts:
  KY-021 Mini Magnetic Reed Switch Module: KY-021 magnetic reed switch module. A reed switch is a magnetic sensor that is normally open and gets closed when exposed to a magnetic field.
