# Fritzing sketch postbox-monitor (saved by Fritzing 0.9.3b)
perfboards: 1

parts:
  VCC1 = 4 x AAA Battery Mount
  R1 = Resistor [tolerance=±5% resistance=1M package=THT]
  R2 = Resistor [tolerance=±5% resistance=1M package=THT]
  S1 = Pushbutton [package=THT]
  S2 = Pushbutton [package=THT]
  R3 = Resistor [tolerance=±5% resistance=1M package=THT]
  R4 = Resistor [tolerance=±5% resistance=1M package=THT]

nets:
  N1: VCC1.-, R2.Pin_0, S1.leg0, S2.leg0
  N2: VCC1.+, R1.Pin_1
  N3: R1.Pin_0, R2.Pin_1
  N4: S1.leg1, R4.Pin_0
  N5: S2.leg1, R3.Pin_0
  N6: R3.Pin_1, R4.Pin_1

notes:
  A2
  Flap
  Door
  A0
  A1
  3V3
  2x 1MΩ
  4.8V
